# Fritzing sketch VOC wiring with raspberry pi (saved by Fritzing 0.9.3b)
circuit board: 5.21342cm x 3.54939cm
breadboards: 1

parts:
  Raspberry_Pi_1 = Raspberry Pi 3 [part_number=RPI-3-V1.2]
  SparkFun_CSS811_Breakout1 = SparkFun_CSS811_Breakout [part_number=14193]

nets:
  3V3: Raspberry_Pi_1.3v3, SparkFun_CSS811_Breakout1.3.3V
  N1: Raspberry_Pi_1.GPIO2, SparkFun_CSS811_Breakout1.SDA
  N2: Raspberry_Pi_1.GPIO3, SparkFun_CSS811_Breakout1.SCL
  GND: Raspberry_Pi_1.GND, SparkFun_CSS811_Breakout1.!WAKE, SparkFun_CSS811_Breakout1.GND

notes:
  Princess H.

custom parts:
  SparkFun_CSS811_Breakout: The CCS811 Air Quality Breakout is a digital gas sensor solution that senses a wide range of Total Volatile Organic Compounds (TVOCs), including equivalent carbon dioxide (eCO2) and metal oxide (MOX) levels. VOCs are often categorized as pollutants and/or sensory irritants and can come from a variety of sources like construction materials (paint, carpet, etc.), machines (copiers, processors,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
